# Fritzing sketch ADXL (saved by Fritzing 0.9.0b)

parts:
  Part1 = Arduino Mega 2560 (Rev3)
  Part2 = Triple Axis Accelerometer Breakout - ADXL335

nets:
  N1: Part1.A0, Part2.ZOUT
  N2: Part1.A1, Part2.YOUT
  N3: Part1.A2, Part2.XOUT
  5V: Part1.5V, Part2.VCC
  GND: Part1.GND, Part2.GND
