# Fritzing sketch Untitled Sketch 2 (saved by Fritzing 0.9.0b)

parts:
  Part1 = Arduino Mega 2560 (Rev3)
  Part2 = SRF05 Ultrasonic Rangefinder

nets:
  N1: Part1.D8_PWM, Part2.Trig
  GND: Part1.GND, Part2.GND
  N2: Part1.D7_PWM, Part2.Echo
